# Fritzing sketch MittBlockSchema (saved by Fritzing 0.9.3b)
breadboards: 1

parts:
  Part1 = Arduino Uno (Rev3)
  LED1 = LED - 5mm [color="Red (633nm)" package="5 mm [THT]"]
  T1 = LM35 Temperature Sensor [package="TO92 [THT]"]
  R1 = Resistor [tolerance=±5% resistance=220 package=THT]
  R2 = Resistor [tolerance=±5% resistance=220 package=THT]

nets:
  N1: Part1.A0, LED1.anode
  N2: Part1.D7, T1.+Vs, R1.Pin_1
  N3: Part1.5V, T1.Vout, R1.Pin_0, R2.Pin_0
  GND: Part1.GND, T1.GND
  N4: LED1.cathode, R2.Pin_1
